# Fritzing sketch MotionPet_estagioC (saved by Fritzing 1.0.5)
breadboards: 1

parts:
  U1 = ESP32 DevKit 38 pinos (generico MotionPet)
  M1 = HC-SR04 Ultrasonic Distance Sensor
  R1 = Resistor [resistance=2200 package=THT]
  R2 = Resistor [resistance=3300 package=THT]
  M2 = Modulo TCRT5000 (comparador LM393) 4 pinos
  P1 = Potenciometro rotativo 3 terminais

nets:
  N1: U1.GND#J3.7, M1.GND, R2.Pin_0
  N2: U1.IO5, M1.TRIG
  3V3: U1.3V3, M2.VCC, P1.END_A
  N3: U1.VP, P1.WIPER
  N4: U1.IO34, R1.Pin_1, R2.Pin_1
  N5: U1.IO35, M2.DO
  N6: U1.GND#J2.14, M2.GND, P1.END_B
  5V: U1.5V, M1.VCC
  N7: M1.ECHO, R1.Pin_0

custom parts:
  ESP32 DevKit 38 pinos (generico MotionPet): Parte generica: pinagem tipo DevKitC V4, 0,9 pol entre fileiras. NAO e o modelo exato da sua placa.
  Modulo TCRT5000 (comparador LM393) 4 pinos: Parte generica: Modulo TCRT5000 (comparador LM393) 4 pinos. Ordem dos pinos: ['VCC', 'GND', 'DO', 'AO'].
  Potenciometro rotativo 3 terminais: Parte generica: Potenciometro rotativo 3 terminais. Ordem dos pinos: ['END_A', 'WIPER', 'END_B'].
